# Fritzing sketch circut_reed (saved by Fritzing 0.9.3b)
breadboards: 1

parts:
  S1 = Reed switch [package=THT]
  R1 = Resistor [tolerance=±5% resistance=220 package=THT]
  LED1 = LED - 5mm [color="Red (633nm)" package="5 mm [THT]"]
  VCC1 = 4 x AAA Battery Mount

nets:
  N1: S1.pin_1, VCC1.-
  N2: S1.pin_2, LED1.cathode
  N3: R1.Pin_0, LED1.anode
  N4: R1.Pin_1, VCC1.+
